// Digital circuit ANDer.dig as structural Verilog
module ANDer (
  input  [7:0] i,
  input  e,
  input  [7:0] i2,
  output [7:0] o
);

  wire [7:0] and_3_out, enabler_and_1_o, enabler_and_2_o;

  enabler_and enabler_and_1 (.o(enabler_and_1_o), .i(i), .e(e));
  enabler_and enabler_and_2 (.o(enabler_and_2_o), .i(i2), .e(e));
  and and_1 (and_3_out[0], enabler_and_2_o[0], enabler_and_1_o[0]);
  and and_2 (and_3_out[1], enabler_and_2_o[1], enabler_and_1_o[1]);
  and and_3 (and_3_out[2], enabler_and_2_o[2], enabler_and_1_o[2]);
  and and_4 (and_3_out[3], enabler_and_2_o[3], enabler_and_1_o[3]);
  and and_5 (and_3_out[4], enabler_and_2_o[4], enabler_and_1_o[4]);
  and and_6 (and_3_out[5], enabler_and_2_o[5], enabler_and_1_o[5]);
  and and_7 (and_3_out[6], enabler_and_2_o[6], enabler_and_1_o[6]);
  and and_8 (and_3_out[7], enabler_and_2_o[7], enabler_and_1_o[7]);
  enabler_high_impedance enabler_high_impedance_1 (.o(o), .i(and_3_out), .e(e));
endmodule
