// Digital circuit ORer.dig as structural Verilog
module ORer (
  input  [7:0] i,
  input  e,
  input  [7:0] i2,
  output [7:0] o
);

  wire [7:0] enabler_and_1_o, enabler_and_2_o, or_2_out;

  enabler_and enabler_and_1 (.o(enabler_and_1_o), .i(i), .e(e));
  enabler_and enabler_and_2 (.o(enabler_and_2_o), .i(i2), .e(e));
  or or_1 (or_2_out[0], enabler_and_2_o[0], enabler_and_1_o[0]);
  or or_2 (or_2_out[1], enabler_and_2_o[1], enabler_and_1_o[1]);
  or or_3 (or_2_out[2], enabler_and_2_o[2], enabler_and_1_o[2]);
  or or_4 (or_2_out[3], enabler_and_2_o[3], enabler_and_1_o[3]);
  or or_5 (or_2_out[4], enabler_and_2_o[4], enabler_and_1_o[4]);
  or or_6 (or_2_out[5], enabler_and_2_o[5], enabler_and_1_o[5]);
  or or_7 (or_2_out[6], enabler_and_2_o[6], enabler_and_1_o[6]);
  or or_8 (or_2_out[7], enabler_and_2_o[7], enabler_and_1_o[7]);
  enabler_high_impedance enabler_high_impedance_1 (.o(o), .i(or_2_out), .e(e));
endmodule
