// Digital circuit main.dig as structural Verilog
module main (
  input  in_1,
  input  in_2,
  input  in_3,
  input  in_4,
  input  in_5,
  input  in_6,
  input  in_7,
  input  in_8,
  input  in_9,
  input  in_10,
  input  in_11
);

  wire [3:0] R0_out, R0_out_2;
  wire [7:0] MAR_out;

  Seven_Seg_Hex seven_seg_hex_1 (.d(R0_out_2), .dp(1'b0));
  Seven_Seg_Hex seven_seg_hex_2 (.d(R0_out), .dp(1'b0));
  registro R0 (.in({R0_out_2, R0_out}), .out({R0_out_2, R0_out}), .s(in_1), .e(in_2));
  registro R1 (.in({R0_out_2, R0_out}), .out({R0_out_2, R0_out}), .s(in_3), .e(in_4));
  registro R2 (.in({R0_out_2, R0_out}), .out({R0_out_2, R0_out}), .s(in_5), .e(in_6));
  registro R3 (.in({R0_out_2, R0_out}), .out({R0_out_2, R0_out}), .s(in_7), .e(in_8));
  MAR MAR (.out(MAR_out), .in({R0_out_2, R0_out}), .s(in_9));
  RAM RAM (.a(MAR_out), .s(in_10), .e(in_11), .o({R0_out_2, R0_out}), .i({R0_out_2, R0_out}));
  Seven_Seg_Hex seven_seg_hex_3 (.d(MAR_out[7:4]), .dp(1'b0));
  Seven_Seg_Hex seven_seg_hex_4 (.d(MAR_out[3:0]), .dp(1'b0));

  // Notes on the sheet:
  //   Datos del bus
  //   Address
endmodule
