// Digital circuit main_PC_clark.dig as structural Verilog
module main_PC_clark (
  input  [7:0] address,
  input  [7:0] input_bus,
  input  clk
);

  wire button_1_out, button_2_out, button_3_out;
  wire [3:0] ram_1_o, ram_1_o_2;
  wire [7:0] mar_1_out;

  Seven_Seg_Hex seven_seg_hex_1 (.d(input_bus[7:4]), .dp(1'b0));
  Seven_Seg_Hex seven_seg_hex_2 (.d(input_bus[3:0]), .dp(1'b0));
  Button button_1 (.out(button_1_out));
  Button button_2 (.out(button_2_out));
  Button button_3 (.out(button_3_out));
  MAR mar_1 (.in(address), .s(button_1_out), .out(mar_1_out));
  RAM ram_1 (.a(mar_1_out), .e(button_2_out), .s(button_3_out), .i(input_bus), .o({ram_1_o_2, ram_1_o}));
  Seven_Seg_Hex seven_seg_hex_3 (.d(ram_1_o_2), .dp(1'b0));
  Seven_Seg_Hex seven_seg_hex_4 (.d(ram_1_o), .dp(1'b0));
endmodule
