// Digital circuit registro.dig as structural Verilog
module registro (
  input  [7:0] in,
  input  s,
  input  e,
  output [7:0] out
);

  // mem_1byte mem_1byte_1: pin names not known; wires that end beside it: s, e
endmodule
