// Digital circuit main_PC_clark.dig as structural Verilog
module main_PC_clark (
  input  in_1,
  input  in_2,
  input  [7:0] in_3,
  input  in_4
);

  registro registro_1 (.in(in_3), .s(in_1), .e(in_2), .out(in_3));
  registro registro_2 (.in(in_3), .s(in_1), .e(in_2), .out(in_3));
  Seven_Seg_Hex seven_seg_hex_1 (.d(in_3[3:0]), .dp(in_4));
  Seven_Seg_Hex seven_seg_hex_2 (.d(in_3[7:4]), .dp(in_4));
endmodule
