// Digital circuit mem_1byte.dig as structural Verilog
module mem_1byte (
  input  i,
  input  i_2,
  input  i_3,
  input  i_4,
  input  i_5,
  input  i_6,
  input  i_7,
  input  i_8,
  input  s,
  output o,
  output o_2,
  output o_3,
  output o_4,
  output o_5,
  output o_6,
  output o_7,
  output o_8
);

  mem_1bit mem_1bit_1 (.i(i), .s(s), .o(o));
  mem_1bit mem_1bit_2 (.i(i_2), .s(s), .o(o_2));
  mem_1bit mem_1bit_3 (.i(i_3), .s(s), .o(o_3));
  mem_1bit mem_1bit_4 (.i(i_4), .s(s), .o(o_4));
  mem_1bit mem_1bit_5 (.i(i_5), .s(s), .o(o_5));
  mem_1bit mem_1bit_6 (.i(i_6), .s(s), .o(o_6));
  mem_1bit mem_1bit_7 (.i(i_7), .s(s), .o(o_7));
  mem_1bit mem_1bit_8 (.i(i_8), .s(s), .o(o_8));
endmodule
