// Logisim project computer_clark.circ as structural Verilog
module pruebas_dispositivos (
  input  in_1,
  input  in_2,
  input  in_3,
  input  [7:0] in_4,
  input  in_5,
  input  in_6
);

  wire dipswitch_1_p1, dipswitch_1_p2, dipswitch_1_p3, dipswitch_1_p4, dipswitch_1_p5, dipswitch_1_p6,
       dipswitch_1_p7, dipswitch_1_p8, mem_bit_1_out_3, mem_byte_1_out_10, mem_byte_1_out_11,
       mem_byte_1_out_12, mem_byte_1_out_13, mem_byte_1_out_14, mem_byte_1_out_15, mem_byte_1_out_16,
       mem_byte_1_out_17;

  LED led_1 (.in(mem_bit_1_out_3));
  mem_bit mem_bit_1 (.set(in_2), .data(in_1), .out_3(mem_bit_1_out_3));
  // DipSwitch dipswitch_1: pin names not known; wires that end beside it: dipswitch_1_p1, dipswitch_1_p2, dipswitch_1_p3, dipswitch_1_p4, dipswitch_1_p5, dipswitch_1_p6, dipswitch_1_p7, dipswitch_1_p8
  mem_byte mem_byte_1 (
    .set(in_3), .in_2(dipswitch_1_p2), .in_3(dipswitch_1_p3), .in_4(dipswitch_1_p4), .in_5(dipswitch_1_p5),
    .in_6(dipswitch_1_p6), .in_7(dipswitch_1_p7), .in_8(dipswitch_1_p8), .in_1(dipswitch_1_p1),
    .out_11(mem_byte_1_out_11), .out_12(mem_byte_1_out_12), .out_13(mem_byte_1_out_13),
    .out_14(mem_byte_1_out_14), .out_15(mem_byte_1_out_15), .out_16(mem_byte_1_out_16),
    .out_17(mem_byte_1_out_17), .out_10(mem_byte_1_out_10));
  LedBar ledbar_1 (
    .led0(mem_byte_1_out_10), .led1(mem_byte_1_out_11), .led2(mem_byte_1_out_12), .led3(mem_byte_1_out_13),
    .led4(mem_byte_1_out_14), .led5(mem_byte_1_out_15), .led6(mem_byte_1_out_16), .led7(mem_byte_1_out_17));
  register_nand_conbus register_nand_conbus_1 (.input_data(in_4), .set(in_5), .enable(in_6));  // open: output_data

  // Notes on the sheet:
  //   Memoria de 1 bit
  //   Memoria de 1 byte
  //   Registro de 1 byte
endmodule

module pruebas_copy_registros (
  input  [7:0] in_1,
  input  in_2,
  input  in_3,
  input  in_4,
  input  in_5,
  input  in_6,
  output [7:0] out_7
);

  wire button_1_out, button_2_out, button_3_out, button_4_out, button_5_out;

  register_visor register_visor_1 (.input_data(in_1), .set(button_1_out), .enable(in_2), .output_data(out_7));
  Button button_1 (.out(button_1_out));
  register_visor register_visor_2 (.input_data(out_7), .set(button_2_out), .enable(in_3), .output_data(out_7));
  Button button_2 (.out(button_2_out));
  register_visor register_visor_3 (.input_data(out_7), .set(button_3_out), .enable(in_4), .output_data(out_7));
  Button button_3 (.out(button_3_out));
  register_visor register_visor_4 (.input_data(out_7), .set(button_4_out), .enable(in_5), .output_data(out_7));
  Button button_4 (.out(button_4_out));
  Button button_5 (.out(button_5_out));
  register_visor register_visor_5 (.input_data(out_7), .set(button_5_out), .enable(in_6), .output_data(out_7));
  Pull_Resistor pull_resistor_1 (.node(out_7));

  // Notes on the sheet:
  //   Prueba de concepto de grabación de bytes de un registro a otro
endmodule

module RAM_clark (
);

  wire undriven, undriven_2, undriven_4, undriven_5, undriven_7, undriven_8, undriven_10, undriven_11,
       undriven_13, undriven_14, undriven_15, undriven_16, undriven_17, undriven_18, undriven_19,
       undriven_20, undriven_21, undriven_22, undriven_23, undriven_24, undriven_25, undriven_26,
       undriven_27, undriven_28, undriven_29, undriven_30, undriven_31, undriven_32;
  wire [7:0] undriven_3, undriven_6, undriven_9, undriven_12;

  registro_RAM registro_ram_1 (
    .input_bus(undriven_3), .vertical_wire(undriven_13), .horizontal_wire(undriven_18), .enabler(undriven),
    .set(undriven_2), .output_bus(undriven_3));
  registro_RAM registro_ram_2 (
    .input_bus(undriven_6), .vertical_wire(undriven_13), .horizontal_wire(undriven_19), .enabler(undriven_4),
    .set(undriven_5), .output_bus(undriven_6));
  registro_RAM registro_ram_3 (
    .input_bus(undriven_9), .vertical_wire(undriven_13), .horizontal_wire(undriven_20), .enabler(undriven_7),
    .set(undriven_8), .output_bus(undriven_9));
  registro_RAM registro_ram_4 (
    .input_bus(undriven_12), .vertical_wire(undriven_13), .horizontal_wire(undriven_21),
    .enabler(undriven_10), .set(undriven_11), .output_bus(undriven_12));
  registro_RAM registro_ram_5 (
    .input_bus(undriven_3), .vertical_wire(undriven_14), .horizontal_wire(undriven_18), .enabler(undriven),
    .set(undriven_2), .output_bus(undriven_3));
  registro_RAM registro_ram_6 (
    .input_bus(undriven_6), .vertical_wire(undriven_14), .horizontal_wire(undriven_19), .enabler(undriven_4),
    .set(undriven_5), .output_bus(undriven_6));
  registro_RAM registro_ram_7 (
    .input_bus(undriven_9), .vertical_wire(undriven_14), .horizontal_wire(undriven_20), .enabler(undriven_7),
    .set(undriven_8), .output_bus(undriven_9));
  registro_RAM registro_ram_8 (
    .input_bus(undriven_12), .vertical_wire(undriven_14), .horizontal_wire(undriven_21),
    .enabler(undriven_10), .set(undriven_11), .output_bus(undriven_12));
  registro_RAM registro_ram_9 (
    .input_bus(undriven_3), .vertical_wire(undriven_15), .horizontal_wire(undriven_18), .enabler(undriven),
    .set(undriven_2), .output_bus(undriven_3));
  registro_RAM registro_ram_10 (
    .input_bus(undriven_6), .vertical_wire(undriven_15), .horizontal_wire(undriven_19), .enabler(undriven_4),
    .set(undriven_5), .output_bus(undriven_6));
  registro_RAM registro_ram_11 (
    .input_bus(undriven_9), .vertical_wire(undriven_15), .horizontal_wire(undriven_20), .enabler(undriven_7),
    .set(undriven_8), .output_bus(undriven_9));
  registro_RAM registro_ram_12 (
    .input_bus(undriven_12), .vertical_wire(undriven_15), .horizontal_wire(undriven_21),
    .enabler(undriven_10), .set(undriven_11), .output_bus(undriven_12));
  registro_RAM registro_ram_13 (
    .input_bus(undriven_3), .vertical_wire(undriven_16), .horizontal_wire(undriven_18), .enabler(undriven),
    .set(undriven_2), .output_bus(undriven_3));
  registro_RAM registro_ram_14 (
    .input_bus(undriven_6), .vertical_wire(undriven_16), .horizontal_wire(undriven_19), .enabler(undriven_4),
    .set(undriven_5), .output_bus(undriven_6));
  registro_RAM registro_ram_15 (
    .input_bus(undriven_9), .vertical_wire(undriven_16), .horizontal_wire(undriven_20), .enabler(undriven_7),
    .set(undriven_8), .output_bus(undriven_9));
  registro_RAM registro_ram_16 (
    .input_bus(undriven_12), .vertical_wire(undriven_16), .horizontal_wire(undriven_21),
    .enabler(undriven_10), .set(undriven_11), .output_bus(undriven_12));
  registro_RAM registro_ram_17 (
    .input_bus(undriven_3), .vertical_wire(undriven_17), .horizontal_wire(undriven_18), .enabler(undriven),
    .set(undriven_2), .output_bus(undriven_3));
  registro_RAM registro_ram_18 (
    .input_bus(undriven_6), .vertical_wire(undriven_17), .horizontal_wire(undriven_19), .enabler(undriven_4),
    .set(undriven_5), .output_bus(undriven_6));
  registro_RAM registro_ram_19 (
    .input_bus(undriven_9), .vertical_wire(undriven_17), .horizontal_wire(undriven_20), .enabler(undriven_7),
    .set(undriven_8), .output_bus(undriven_9));
  registro_RAM registro_ram_20 (
    .input_bus(undriven_12), .vertical_wire(undriven_17), .horizontal_wire(undriven_21),
    .enabler(undriven_10), .set(undriven_11), .output_bus(undriven_12));
  registro_RAM registro_ram_21 (
    .input_bus(undriven_3), .vertical_wire(undriven_22), .horizontal_wire(undriven_18), .enabler(undriven),
    .set(undriven_2), .output_bus(undriven_3));
  registro_RAM registro_ram_22 (
    .input_bus(undriven_6), .vertical_wire(undriven_22), .horizontal_wire(undriven_19), .enabler(undriven_4),
    .set(undriven_5), .output_bus(undriven_6));
  registro_RAM registro_ram_23 (
    .input_bus(undriven_9), .vertical_wire(undriven_22), .horizontal_wire(undriven_20), .enabler(undriven_7),
    .set(undriven_8), .output_bus(undriven_9));
  registro_RAM registro_ram_24 (
    .input_bus(undriven_12), .vertical_wire(undriven_22), .horizontal_wire(undriven_21),
    .enabler(undriven_10), .set(undriven_11), .output_bus(undriven_12));
  registro_RAM registro_ram_25 (
    .input_bus(undriven_3), .vertical_wire(undriven_23), .horizontal_wire(undriven_18), .enabler(undriven),
    .set(undriven_2), .output_bus(undriven_3));
  registro_RAM registro_ram_26 (
    .input_bus(undriven_6), .vertical_wire(undriven_23), .horizontal_wire(undriven_19), .enabler(undriven_4),
    .set(undriven_5), .output_bus(undriven_6));
  registro_RAM registro_ram_27 (
    .input_bus(undriven_9), .vertical_wire(undriven_23), .horizontal_wire(undriven_20), .enabler(undriven_7),
    .set(undriven_8), .output_bus(undriven_9));
  registro_RAM registro_ram_28 (
    .input_bus(undriven_12), .vertical_wire(undriven_23), .horizontal_wire(undriven_21),
    .enabler(undriven_10), .set(undriven_11), .output_bus(undriven_12));
  registro_RAM registro_ram_29 (
    .input_bus(undriven_3), .vertical_wire(undriven_24), .horizontal_wire(undriven_18), .enabler(undriven),
    .set(undriven_2), .output_bus(undriven_3));
  registro_RAM registro_ram_30 (
    .input_bus(undriven_6), .vertical_wire(undriven_24), .horizontal_wire(undriven_19), .enabler(undriven_4),
    .set(undriven_5), .output_bus(undriven_6));
  registro_RAM registro_ram_31 (
    .input_bus(undriven_9), .vertical_wire(undriven_24), .horizontal_wire(undriven_20), .enabler(undriven_7),
    .set(undriven_8), .output_bus(undriven_9));
  registro_RAM registro_ram_32 (
    .input_bus(undriven_12), .vertical_wire(undriven_24), .horizontal_wire(undriven_21),
    .enabler(undriven_10), .set(undriven_11), .output_bus(undriven_12));
  registro_RAM registro_ram_33 (
    .input_bus(undriven_3), .vertical_wire(undriven_25), .horizontal_wire(undriven_18), .enabler(undriven),
    .set(undriven_2), .output_bus(undriven_3));
  registro_RAM registro_ram_34 (
    .input_bus(undriven_6), .vertical_wire(undriven_25), .horizontal_wire(undriven_19), .enabler(undriven_4),
    .set(undriven_5), .output_bus(undriven_6));
  registro_RAM registro_ram_35 (
    .input_bus(undriven_9), .vertical_wire(undriven_25), .horizontal_wire(undriven_20), .enabler(undriven_7),
    .set(undriven_8), .output_bus(undriven_9));
  registro_RAM registro_ram_36 (
    .input_bus(undriven_12), .vertical_wire(undriven_25), .horizontal_wire(undriven_21),
    .enabler(undriven_10), .set(undriven_11), .output_bus(undriven_12));
  registro_RAM registro_ram_37 (
    .input_bus(undriven_3), .vertical_wire(undriven_26), .horizontal_wire(undriven_18), .enabler(undriven),
    .set(undriven_2), .output_bus(undriven_3));
  registro_RAM registro_ram_38 (
    .input_bus(undriven_6), .vertical_wire(undriven_26), .horizontal_wire(undriven_19), .enabler(undriven_4),
    .set(undriven_5), .output_bus(undriven_6));
  registro_RAM registro_ram_39 (
    .input_bus(undriven_9), .vertical_wire(undriven_26), .horizontal_wire(undriven_20), .enabler(undriven_7),
    .set(undriven_8), .output_bus(undriven_9));
  registro_RAM registro_ram_40 (
    .input_bus(undriven_12), .vertical_wire(undriven_26), .horizontal_wire(undriven_21),
    .enabler(undriven_10), .set(undriven_11), .output_bus(undriven_12));
  registro_RAM registro_ram_41 (
    .input_bus(undriven_3), .vertical_wire(undriven_27), .horizontal_wire(undriven_18), .enabler(undriven),
    .set(undriven_2), .output_bus(undriven_3));
  registro_RAM registro_ram_42 (
    .input_bus(undriven_6), .vertical_wire(undriven_27), .horizontal_wire(undriven_19), .enabler(undriven_4),
    .set(undriven_5), .output_bus(undriven_6));
  registro_RAM registro_ram_43 (
    .input_bus(undriven_9), .vertical_wire(undriven_27), .horizontal_wire(undriven_20), .enabler(undriven_7),
    .set(undriven_8), .output_bus(undriven_9));
  registro_RAM registro_ram_44 (
    .input_bus(undriven_12), .vertical_wire(undriven_27), .horizontal_wire(undriven_21),
    .enabler(undriven_10), .set(undriven_11), .output_bus(undriven_12));
  registro_RAM registro_ram_45 (
    .input_bus(undriven_3), .vertical_wire(undriven_28), .horizontal_wire(undriven_18), .enabler(undriven),
    .set(undriven_2), .output_bus(undriven_3));
  registro_RAM registro_ram_46 (
    .input_bus(undriven_6), .vertical_wire(undriven_28), .horizontal_wire(undriven_19), .enabler(undriven_4),
    .set(undriven_5), .output_bus(undriven_6));
  registro_RAM registro_ram_47 (
    .input_bus(undriven_9), .vertical_wire(undriven_28), .horizontal_wire(undriven_20), .enabler(undriven_7),
    .set(undriven_8), .output_bus(undriven_9));
  registro_RAM registro_ram_48 (
    .input_bus(undriven_12), .vertical_wire(undriven_28), .horizontal_wire(undriven_21),
    .enabler(undriven_10), .set(undriven_11), .output_bus(undriven_12));
  registro_RAM registro_ram_49 (
    .input_bus(undriven_3), .vertical_wire(undriven_29), .horizontal_wire(undriven_18), .enabler(undriven),
    .set(undriven_2), .output_bus(undriven_3));
  registro_RAM registro_ram_50 (
    .input_bus(undriven_6), .vertical_wire(undriven_29), .horizontal_wire(undriven_19), .enabler(undriven_4),
    .set(undriven_5), .output_bus(undriven_6));
  registro_RAM registro_ram_51 (
    .input_bus(undriven_9), .vertical_wire(undriven_29), .horizontal_wire(undriven_20), .enabler(undriven_7),
    .set(undriven_8), .output_bus(undriven_9));
  registro_RAM registro_ram_52 (
    .input_bus(undriven_12), .vertical_wire(undriven_29), .horizontal_wire(undriven_21),
    .enabler(undriven_10), .set(undriven_11), .output_bus(undriven_12));
  registro_RAM registro_ram_53 (
    .input_bus(undriven_3), .vertical_wire(undriven_30), .horizontal_wire(undriven_18), .enabler(undriven),
    .set(undriven_2), .output_bus(undriven_3));
  registro_RAM registro_ram_54 (
    .input_bus(undriven_6), .vertical_wire(undriven_30), .horizontal_wire(undriven_19), .enabler(undriven_4),
    .set(undriven_5), .output_bus(undriven_6));
  registro_RAM registro_ram_55 (
    .input_bus(undriven_9), .vertical_wire(undriven_30), .horizontal_wire(undriven_20), .enabler(undriven_7),
    .set(undriven_8), .output_bus(undriven_9));
  registro_RAM registro_ram_56 (
    .input_bus(undriven_12), .vertical_wire(undriven_30), .horizontal_wire(undriven_21),
    .enabler(undriven_10), .set(undriven_11), .output_bus(undriven_12));
  registro_RAM registro_ram_57 (
    .input_bus(undriven_3), .vertical_wire(undriven_31), .horizontal_wire(undriven_18), .enabler(undriven),
    .set(undriven_2), .output_bus(undriven_3));
  registro_RAM registro_ram_58 (
    .input_bus(undriven_6), .vertical_wire(undriven_31), .horizontal_wire(undriven_19), .enabler(undriven_4),
    .set(undriven_5), .output_bus(undriven_6));
  registro_RAM registro_ram_59 (
    .input_bus(undriven_9), .vertical_wire(undriven_31), .horizontal_wire(undriven_20), .enabler(undriven_7),
    .set(undriven_8), .output_bus(undriven_9));
  registro_RAM registro_ram_60 (
    .input_bus(undriven_12), .vertical_wire(undriven_31), .horizontal_wire(undriven_21),
    .enabler(undriven_10), .set(undriven_11), .output_bus(undriven_12));
  registro_RAM registro_ram_61 (
    .input_bus(undriven_3), .vertical_wire(undriven_32), .horizontal_wire(undriven_18), .enabler(undriven),
    .set(undriven_2), .output_bus(undriven_3));
  registro_RAM registro_ram_62 (
    .input_bus(undriven_6), .vertical_wire(undriven_32), .horizontal_wire(undriven_19), .enabler(undriven_4),
    .set(undriven_5), .output_bus(undriven_6));
  registro_RAM registro_ram_63 (
    .input_bus(undriven_9), .vertical_wire(undriven_32), .horizontal_wire(undriven_20), .enabler(undriven_7),
    .set(undriven_8), .output_bus(undriven_9));
  registro_RAM registro_ram_64 (
    .input_bus(undriven_12), .vertical_wire(undriven_32), .horizontal_wire(undriven_21),
    .enabler(undriven_10), .set(undriven_11), .output_bus(undriven_12));
endmodule

module registro_RAM (
  input  [7:0] input_bus,
  input  [7:0] output_bus,
  input  enabler,
  input  vertical_wire,
  input  set,
  input  horizontal_wire
);

  wire and_nand_small_1_out_3, and_nand_small_2_out_3, and_nand_small_3_out_3;

  register_nand_conbus register_nand_conbus_1 (
    .input_data(input_bus), .set(and_nand_small_1_out_3), .enable(and_nand_small_2_out_3),
    .output_data(output_bus));
  and_nand_small and_nand_small_1 (.in_1(and_nand_small_3_out_3), .in_2(set), .out_3(and_nand_small_1_out_3));
  and_nand_small and_nand_small_2 (.in_1(and_nand_small_3_out_3), .in_2(enabler), .out_3(and_nand_small_2_out_3));
  and_nand_small and_nand_small_3 (.in_1(vertical_wire), .in_2(horizontal_wire), .out_3(and_nand_small_3_out_3));
endmodule

module register_visor (
  input  [7:0] input_data,
  input  set,
  input  enable,
  output [7:0] output_data
);

  wire [7:0] mem_byte_1_out_10;

  mem_byte mem_byte_1 (
    .set(set), .in_2(input_data[1]), .in_3(input_data[2]), .in_4(input_data[3]), .in_5(input_data[4]),
    .in_6(input_data[5]), .in_7(input_data[6]), .in_8(input_data[7]), .in_1(input_data[0]),
    .out_11(mem_byte_1_out_10[1]), .out_12(mem_byte_1_out_10[2]), .out_13(mem_byte_1_out_10[3]),
    .out_14(mem_byte_1_out_10[4]), .out_15(mem_byte_1_out_10[5]), .out_16(mem_byte_1_out_10[6]),
    .out_17(mem_byte_1_out_10[7]), .out_10(mem_byte_1_out_10[0]));
  enabler_8bits enabler_8bits_1 (
    .in_2(mem_byte_1_out_10[1]), .in_3(mem_byte_1_out_10[2]), .in_4(mem_byte_1_out_10[3]),
    .in_5(mem_byte_1_out_10[4]), .in_6(mem_byte_1_out_10[5]), .in_7(mem_byte_1_out_10[6]),
    .in_8(mem_byte_1_out_10[7]), .in_1(mem_byte_1_out_10[0]), .in_9(enable), .out_11(output_data[1]),
    .out_12(output_data[2]), .out_13(output_data[3]), .out_14(output_data[4]), .out_15(output_data[5]),
    .out_16(output_data[6]), .out_17(output_data[7]), .out_10(output_data[0]));
  Hex_Digit_Display hex_digit_display_1 (.value(mem_byte_1_out_10[3:0]));  // open: dp
  Hex_Digit_Display hex_digit_display_2 (.value(mem_byte_1_out_10[7:4]));  // open: dp
endmodule

module register_nand_conbus (
  input  [7:0] input_data,
  input  set,
  input  enable,
  output [7:0] output_data
);

  wire mem_byte_1_out_10, mem_byte_1_out_11, mem_byte_1_out_12, mem_byte_1_out_13, mem_byte_1_out_14,
       mem_byte_1_out_15, mem_byte_1_out_16, mem_byte_1_out_17;

  mem_byte mem_byte_1 (
    .set(set), .in_2(input_data[1]), .in_3(input_data[2]), .in_4(input_data[3]), .in_5(input_data[4]),
    .in_6(input_data[5]), .in_7(input_data[6]), .in_8(input_data[7]), .in_1(input_data[0]),
    .out_11(mem_byte_1_out_11), .out_12(mem_byte_1_out_12), .out_13(mem_byte_1_out_13),
    .out_14(mem_byte_1_out_14), .out_15(mem_byte_1_out_15), .out_16(mem_byte_1_out_16),
    .out_17(mem_byte_1_out_17), .out_10(mem_byte_1_out_10));
  enabler_8bits enabler_8bits_1 (
    .in_2(mem_byte_1_out_11), .in_3(mem_byte_1_out_12), .in_4(mem_byte_1_out_13), .in_5(mem_byte_1_out_14),
    .in_6(mem_byte_1_out_15), .in_7(mem_byte_1_out_16), .in_8(mem_byte_1_out_17), .in_1(mem_byte_1_out_10),
    .in_9(enable), .out_11(output_data[1]), .out_12(output_data[2]), .out_13(output_data[3]),
    .out_14(output_data[4]), .out_15(output_data[5]), .out_16(output_data[6]), .out_17(output_data[7]),
    .out_10(output_data[0]));
endmodule

module enabler_8bits (
  input  in_1,
  input  in_2,
  input  in_3,
  input  in_4,
  input  in_5,
  input  in_6,
  input  in_7,
  input  in_8,
  input  in_9,
  output out_10,
  output out_11,
  output out_12,
  output out_13,
  output out_14,
  output out_15,
  output out_16,
  output out_17
);

  buffer_alta_impedancia buffer_alta_impedancia_1 ();  // open: enable, data, out_3
  buffer_alta_impedancia buffer_alta_impedancia_2 (.enable(in_9), .data(in_1), .out_3(out_10));
  buffer_alta_impedancia buffer_alta_impedancia_3 (.enable(in_9), .data(in_2), .out_3(out_11));
  buffer_alta_impedancia buffer_alta_impedancia_4 (.enable(in_9), .data(in_3), .out_3(out_12));
  buffer_alta_impedancia buffer_alta_impedancia_5 (.enable(in_9), .data(in_4), .out_3(out_13));
  buffer_alta_impedancia buffer_alta_impedancia_6 (.enable(in_9), .data(in_5), .out_3(out_14));
  buffer_alta_impedancia buffer_alta_impedancia_7 (.enable(in_9), .data(in_6), .out_3(out_15));
  buffer_alta_impedancia buffer_alta_impedancia_8 (.enable(in_9), .data(in_7), .out_3(out_16));
  buffer_alta_impedancia buffer_alta_impedancia_9 (.enable(in_9), .data(in_8), .out_3(out_17));

  // Notes on the sheet:
  //   input
  //   enabler
  //   output
endmodule

module mem_byte (
  input  in_1,
  input  in_2,
  input  in_3,
  input  in_4,
  input  in_5,
  input  in_6,
  input  in_7,
  input  in_8,
  input  set,
  output out_10,
  output out_11,
  output out_12,
  output out_13,
  output out_14,
  output out_15,
  output out_16,
  output out_17
);

  mem_bit mem_bit_1 (.set(set), .data(in_1), .out_3(out_10));
  mem_bit mem_bit_2 (.set(set), .data(in_2), .out_3(out_11));
  mem_bit mem_bit_3 (.set(set), .data(in_3), .out_3(out_12));
  mem_bit mem_bit_4 (.set(set), .data(in_4), .out_3(out_13));
  mem_bit mem_bit_5 (.set(set), .data(in_5), .out_3(out_14));
  mem_bit mem_bit_6 (.set(set), .data(in_6), .out_3(out_15));
  mem_bit mem_bit_7 (.set(set), .data(in_7), .out_3(out_16));
  mem_bit mem_bit_8 (.set(set), .data(in_8), .out_3(out_17));

  // Notes on the sheet:
  //   input
  //   output
endmodule

module mem_bit (
  input  data,
  input  set,
  output out_3
);

  wire nand_transistors_1_out_3, nand_transistors_2_out_3, nand_transistors_4_out_3, or_nand_1_out_3,
       por_1_out;

  POR #(.PorHighDuration(1)) por_1 (.out(por_1_out));
  or_nand or_nand_1 (.in_1(set), .in_2(por_1_out), .out_3(or_nand_1_out_3));
  nand_transistors nand_transistors_1 (.in_1(data), .in_2(or_nand_1_out_3), .out_3(nand_transistors_1_out_3));
  nand_transistors nand_transistors_2 (
    .in_1(nand_transistors_1_out_3), .in_2(or_nand_1_out_3), .out_3(nand_transistors_2_out_3));
  nand_transistors nand_transistors_3 (.in_1(nand_transistors_1_out_3), .in_2(nand_transistors_4_out_3), .out_3(out_3));
  nand_transistors nand_transistors_4 (.in_1(out_3), .in_2(nand_transistors_2_out_3), .out_3(nand_transistors_4_out_3));

  // Notes on the sheet:
  //   set: pull=up
endmodule

module buffer_alta_impedancia (
  input  data,
  input  enable,
  output out_3
);

  wire nand_transistors_1_out_3, nor_nand_1_out_3, not_nand_1_out_2;

  not_nand not_nand_1 (.in_1(enable), .out_2(not_nand_1_out_2));
  nand_transistors nand_transistors_1 (.in_1(data), .in_2(enable), .out_3(nand_transistors_1_out_3));
  Transistor transistor_1 (.in(1'b1), .out(out_3), .gate(nand_transistors_1_out_3));
  nor_nand nor_nand_1 (.in_1(not_nand_1_out_2), .in_2(data), .out_3(nor_nand_1_out_3));
  Transistor #(.\type ("n")) transistor_2 (.in(1'b0), .out(out_3), .gate(nor_nand_1_out_3));
endmodule

module nor_nand (
  input  in_1,
  input  in_2,
  output out_3
);

  wire or_nand_1_out_3;

  or_nand or_nand_1 (.in_1(in_1), .in_2(in_2), .out_3(or_nand_1_out_3));
  not_nand not_nand_1 (.in_1(or_nand_1_out_3), .out_2(out_3));
endmodule

module or_nand (
  input  in_1,
  input  in_2,
  output out_3
);

  wire not_nand_1_out_2, not_nand_2_out_2;

  not_nand not_nand_1 (.in_1(in_1), .out_2(not_nand_1_out_2));
  not_nand not_nand_2 (.in_1(in_2), .out_2(not_nand_2_out_2));
  nand_transistors nand_transistors_1 (.in_1(not_nand_1_out_2), .in_2(not_nand_2_out_2), .out_3(out_3));
endmodule

module and_nand_small (
  input  in_1,
  input  in_2,
  output out_3
);

  and_nand and_nand_1 (.in_1(in_1), .in_2(in_2), .out_3(out_3));
endmodule

module and_nand (
  input  in_1,
  input  in_2,
  output out_3
);

  wire nand_transistors_1_out_3;

  nand_transistors nand_transistors_1 (.in_1(in_1), .in_2(in_2), .out_3(nand_transistors_1_out_3));
  not_nand not_nand_1 (.in_1(nand_transistors_1_out_3), .out_2(out_3));
endmodule

module not_nand (
  input  in_1,
  output out_2
);

  nand_transistors nand_transistors_1 (.in_1(in_1), .in_2(in_1), .out_3(out_2));
endmodule

module nand_transistors (
  input  in_1,
  input  in_2,
  output out_3
);

  wire transistor_1_out;

  Transistor #(.\type ("n")) transistor_1 (.in(1'b0), .out(transistor_1_out), .gate(in_1));
  Transistor #(.\type ("n")) transistor_2 (.in(transistor_1_out), .out(out_3), .gate(in_2));
  Pull_Resistor #(.pull(1)) pull_resistor_1 (.node(out_3));

  // Notes on the sheet:
  //   in_2: initial=0x1
endmodule

module nand_4_transistors (
  input  in_1,
  input  in_2,
  output out_3
);

  wire transistor_4_out;

  Transistor transistor_1 (.in(1'b1), .out(out_3), .gate(in_1));
  Transistor transistor_2 (.in(1'b1), .out(out_3), .gate(in_2));
  Transistor #(.\type ("n")) transistor_3 (.in(transistor_4_out), .out(out_3), .gate(in_1));
  Transistor #(.\type ("n")) transistor_4 (.in(1'b0), .out(transistor_4_out), .gate(in_2));
endmodule
